# Fritzing sketch GRIS5A-DKb (saved by Fritzing 0.9.3b)
circuit board: 15.8293cm x 11.7244cm
breadboards: 1

parts:
  CD4021B1 = IC, DIP package, 16 pins [chip_label=CD4021B]
  CD4021B3 = IC, DIP package, 16 pins [chip_label=CD4021B]
  LUL = Pushbutton [package="[THT]"]
  LUR = Pushbutton [package="[THT]"]
  LUB = Pushbutton [package="[THT]"]
  LLR = Pushbutton [package="[THT]"]
  LLT = Pushbutton [package="[THT]"]
  LLB = Pushbutton [package="[THT]"]
  LLL = Pushbutton [package="[THT]"]
  LUT = Pushbutton [package="[THT]"]
  RLL = Pushbutton [package="[THT]"]
  RLB = Pushbutton [package="[THT]"]
  RLT = Pushbutton [package="[THT]"]
  RLR = Pushbutton [package="[THT]"]
  RUB = Pushbutton [package="[THT]"]
  RUR = Pushbutton [package="[THT]"]
  RUL = Pushbutton [package="[THT]"]
  CD4021B4 = IC, DIP package, 16 pins [chip_label=CD4021B]
  CD4021B2 = IC, DIP package, 16 pins [chip_label=CD4021B]
  RUT = Pushbutton [package="[THT]"]
  GAL = Pushbutton [package="[THT]"]
  GAB = Pushbutton [package="[THT]"]
  GAT = Pushbutton [package="[THT]"]
  Program_7 = Pushbutton [package="[THT]"]
  Program_6 = Pushbutton [package="[THT]"]
  Program_5 = Pushbutton [package="[THT]"]
  Program_8 = Pushbutton [package="[THT]"]
  Program_4 = Pushbutton [package="[THT]"]
  Program_1 = Pushbutton [package="[THT]"]
  Program_2 = Pushbutton [package="[THT]"]
  Program_3 = Pushbutton [package="[THT]"]
  Preset = Pushbutton [package="[THT]"]
  Play = Pushbutton [package="[THT]"]
  Manual = Pushbutton [package="[THT]"]
  Record = Pushbutton [package="[THT]"]
  LED1 = LED - 5mm [color="Red (633nm)" package="5 mm [THT]"]
  LED2 = LED - 5mm [color="Red (633nm)" package="5 mm [THT]"]
  LED3 = LED - 5mm [color="Red (633nm)" package="5 mm [THT]"]
  LED4 = LED - 5mm [color="Red (633nm)" package="5 mm [THT]"]
  R220 = Resistor [tolerance=±5% resistance=220 package=THT]
  R220_2 = Resistor [tolerance=±5% resistance=220 package=THT]
  R220_3 = Resistor [tolerance=±5% resistance=220 package=THT]
  R220_4 = Resistor [tolerance=±5% resistance=220 package=THT]
  74HC595 = 74HC595 [package="DIP16 [THT]"]
  GAR = Pushbutton [package="[THT]"]
  8R10k1 = mystery part, 9 pins [chip_label=?]
  8R10k3 = mystery part, 9 pins [chip_label=?]
  8R10k4 = mystery part, 9 pins [chip_label=?]
  8R10k2 = mystery part, 9 pins [chip_label=?]

nets:
  N1: CD4021B1.pin1, LUB.Pin_3, LUB.Pin_4, 8R10k1.pin4
  N2: CD4021B1.pin4, LLT.Pin_4, 8R10k1.pin5
  N3: CD4021B1.pin5, LLL.Pin_4, 8R10k1.pin6
  N4: CD4021B1.pin6, LLR.Pin_3, LLR.Pin_4, 8R10k1.pin7
  N5: CD4021B1.pin7, LLB.Pin_3, LLB.Pin_4, 8R10k1.pin8
  N6: CD4021B1.pin8, CD4021B3.pin8, CD4021B4.pin8, CD4021B2.pin8, R220.Pin_1, R220_2.Pin_1, R220_3.Pin_1, R220_4.Pin_1, 74HC595.GND, 74HC595.OE, 8R10k1.pin9, 8R10k3.pin9, 8R10k4.pin1, 8R10k2.pin9
  N7: CD4021B1.pin9, CD4021B3.pin9, CD4021B4.pin9, CD4021B2.pin9
  N8: CD4021B1.pin10, CD4021B3.pin10, CD4021B4.pin10, CD4021B2.pin10
  N9: CD4021B1.pin11, CD4021B3.pin3
  N10: CD4021B1.pin13, LUR.Pin_3, LUR.Pin_4, 8R10k1.pin3
  N11: CD4021B1.pin14, LUL.Pin_3, LUL.Pin_4, 8R10k1.pin2
  N12: CD4021B1.pin15, LUT.Pin_3, LUT.Pin_4, 8R10k1.pin1
  N13: CD4021B1.pin16, CD4021B3.pin16, LUL.Pin_1, LUL.Pin_2, LUR.Pin_1, LUR.Pin_2, LUB.Pin_1, LUB.Pin_2, LLR.Pin_1, LLR.Pin_2, LLT.Pin_1, LLT.Pin_2, LLB.Pin_1, LLB.Pin_2, LLL.Pin_1, LLL.Pin_2, LUT.Pin_1, LUT.Pin_2, RLL.Pin_1, RLL.Pin_2, RLB.Pin_1, RLB.Pin_2, RLT.Pin_1, RLT.Pin_2, RLR.Pin_1, RUB.Pin_1, RUB.Pin_2, RUR.Pin_1, RUR.Pin_2, RUL.Pin_1, RUL.Pin_2, CD4021B4.pin16, CD4021B2.pin16, RUT.Pin_1, RUT.Pin_2, GAL.Pin_1, GAL.Pin_2, GAB.Pin_3, GAB.Pin_4, GAT.Pin_3, GAT.Pin_4, Program_7.Pin_1, Program_6.Pin_1, Program_6.Pin_2, Program_5.Pin_1, Program_5.Pin_2, Program_8.Pin_1, Program_8.Pin_2, Program_4.Pin_1, Program_4.Pin_2, Program_1.Pin_1, Program_1.Pin_2, Program_2.Pin_1, Program_2.Pin_2, Program_3.Pin_1, Program_3.Pin_2, Preset.Pin_1, Preset.Pin_2, Play.Pin_1, Play.Pin_2, Manual.Pin_1, Manual.Pin_2, Record.Pin_1, Record.Pin_2, 74HC595.MR, 74HC595.VCC, GAR.Pin_3, GAR.Pin_4
  N14: CD4021B3.pin1, Play.Pin_3, Play.Pin_4, 8R10k3.pin4
  N15: CD4021B3.pin4, Program_1.Pin_3, Program_1.Pin_4, 8R10k3.pin5
  N16: CD4021B3.pin5, Program_2.Pin_3, Program_2.Pin_4, 8R10k3.pin6
  N17: CD4021B3.pin6, Program_3.Pin_3, Program_3.Pin_4, 8R10k3.pin7
  N18: CD4021B3.pin7, Program_4.Pin_4, 8R10k3.pin8
  N19: CD4021B3.pin11, CD4021B2.pin3
  N20: CD4021B3.pin13, Record.Pin_3, Record.Pin_4, 8R10k3.pin3
  N21: CD4021B3.pin14, Preset.Pin_3, Preset.Pin_4, 8R10k3.pin2
  N22: CD4021B3.pin15, Manual.Pin_3, Manual.Pin_4, 8R10k3.pin1
  N23: RLL.Pin_3, RLL.Pin_4, CD4021B2.pin5, 8R10k2.pin6
  N24: RLB.Pin_3, RLB.Pin_4, CD4021B2.pin7, 8R10k2.pin8
  N25: RLT.Pin_3, RLT.Pin_4, CD4021B2.pin4, 8R10k2.pin5
  N26: RLR.Pin_3, RLR.Pin_4, CD4021B2.pin6, 8R10k2.pin7
  N27: RUB.Pin_3, RUB.Pin_4, CD4021B2.pin1, 8R10k2.pin4
  N28: RUR.Pin_3, RUR.Pin_4, CD4021B2.pin13, 8R10k2.pin3
  N29: RUL.Pin_3, RUL.Pin_4, CD4021B2.pin14, 8R10k2.pin2
  N30: CD4021B4.pin1, Program_8.Pin_3, Program_8.Pin_4, 8R10k4.pin6
  N31: CD4021B4.pin3, CD4021B2.pin11
  N32: CD4021B4.pin4, GAR.Pin_1, GAR.Pin_2, 8R10k4.pin5
  N33: CD4021B4.pin5, GAB.Pin_1, GAB.Pin_2, 8R10k4.pin4
  N34: CD4021B4.pin6, GAT.Pin_1, GAT.Pin_2, 8R10k4.pin3
  N35: CD4021B4.pin7, GAL.Pin_3, GAL.Pin_4, 8R10k4.pin2
  N36: CD4021B4.pin13, Program_7.Pin_3, Program_7.Pin_4, 8R10k4.pin7
  N37: CD4021B4.pin14, Program_6.Pin_3, Program_6.Pin_4, 8R10k4.pin8
  N38: CD4021B4.pin15, Program_5.Pin_3, Program_5.Pin_4, 8R10k4.pin9
  N39: CD4021B2.pin15, RUT.Pin_3, RUT.Pin_4, 8R10k2.pin1
  N40: LED1.cathode, 74HC595.Q1
  N41: LED1.anode, R220.Pin_0
  N42: LED2.cathode, 74HC595.Q0
  N43: LED2.anode, R220_2.Pin_0
  N44: LED3.cathode, 74HC595.Q3
  N45: LED3.anode, R220_3.Pin_0
  N46: LED4.cathode, 74HC595.Q2
  N47: LED4.anode, R220_4.Pin_0

notes:
  GRIS5A DKb r2 (C)
